// Logisim project DISPLAYs - Logisim.circ as structural Verilog: 1 circuit, main circuit Display
module Display (
  input  A1,
  input  B1,
  output A,
  output B,
  output C,
  output D,
  output E,
  output F,
  output G,
  output DP
);

  wire not_1_out, not_2_out, not_3_out, not_4_out, not_5_out, not_6_out, not_8_out, not_9_out;

  not not_1 (not_1_out, A1);
  not not_2 (not_2_out, B1);
  not not_3 (not_3_out, A1);
  not not_4 (not_4_out, B1);
  not not_5 (not_5_out, A1);
  not not_6 (not_6_out, A1);
  not not_7 (E, B1);
  not not_8 (not_8_out, A1);
  not not_9 (not_9_out, B1);
  not not_10 (G, A1);
  or or_1 (DP, B1, A1);
  and and_1 (A, not_1_out, not_2_out);
  or or_2 (B, not_3_out, not_4_out);
  or or_3 (C, not_5_out, B1);
  or or_4 (D, not_6_out, B1);
  and and_2 (F, not_8_out, not_9_out);
endmodule
