// Logisim project LEDs - Logisim.circ as structural Verilog: 1 circuit, main circuit Rock Paper Scissors
module Rock_Paper_Scissors (
  input  A,
  input  B,
  input  C,
  input  D,
  output S1,
  output S2
);

  wire E_out, G_out, H_out, I_out, J_out, K_out, not_1_out, not_2_out, not_3_out, not_4_out, not_5_out,
       not_6_out, not_7_out, not_8_out, O_out, P_out, Q_out, S_out, T_out, U_out, W_out, Y_out;

  not not_1 (not_1_out, A);
  not not_2 (not_2_out, D);
  not not_3 (not_3_out, B);
  not not_4 (not_4_out, C);
  and U (U_out, A, B);
  not not_5 (not_5_out, B);
  not not_6 (not_6_out, C);
  not not_7 (not_7_out, A);
  not not_8 (not_8_out, D);
  and H (H_out, A, B);
  and Q (Q_out, not_1_out, not_2_out);
  or W (W_out, Q_out, E_out);
  and E (E_out, not_3_out, C);
  and T (T_out, B, not_4_out);
  or Y (Y_out, T_out, I_out);
  and I (I_out, U_out, D);
  and O (O_out, not_5_out, not_6_out);
  or P (P_out, O_out, S_out);
  and S (S_out, not_7_out, D);
  and G (G_out, A, not_8_out);
  or J (J_out, G_out, K_out);
  and K (K_out, H_out, C);
  or R (S1, W_out, Y_out);
  or F (S2, P_out, J_out);
endmodule
